# Fritzing sketch Schematic (saved by Fritzing 0.9.3b)
breadboards: 1

parts:
  Part1 = Arduino Uno (Rev3)
  LED1 = RGB LED (com. cathode, rgb) [package="5 mm [THT]"]
  DHT11 = Humidity and Temperature Sensor RHT03
  U1 = 74HC595 [package="DIP16 [THT]"]
  DI1 = 7-Segment LED Display [package=THT]
  DI2 = 7-Segment LED Display [package=THT]
  R1 = Resistor [tolerance=±5% resistance=220 package=THT]
  R2 = Resistor [tolerance=±5% resistance=220 package=THT]
  R3 = Resistor [tolerance=±5% resistance=10k package=THT]  # not connected
  R4 = Resistor [tolerance=±5% resistance=220 package=THT]

nets:
  N1: Part1.D9_PWM, LED1.red_anode
  N2: Part1.D10_PWM/SS, LED1.common_cathode
  N3: Part1.D11_PWM/MOSI, LED1.blue_anode
  N4: Part1.D2, R2.Pin_1
  N5: Part1.D3_PWM, R1.Pin_1
  N6: Part1.D4, DHT11.Data-signal
  N7: Part1.D5_PWM, U1.DS
  N8: Part1.D6_PWM, U1.ST_CP
  N9: Part1.D7, U1.SH_CP
  N10: LED1.green_anode, R4.Pin_1
  N11: DHT11.Vcc, R4.Pin_0
  N12: DHT11.GND_2, U1.GND
  N13: U1.Q1, DI1.cathodeG, DI2.cathodeG
  N14: U1.Q3, DI1.cathodeC, DI2.cathodeC
  N15: U1.Q4, DI1.cathodeE, DI2.cathodeE
  N16: U1.Q5, DI1.cathodeD, DI2.cathodeD
  N17: U1.Q6, DI1.cathodeA, DI2.cathodeA
  N18: U1.Q7, DI1.cathodeB, DI2.cathodeB
  N19: U1.MR, U1.VCC
  N20: U1.Q0, DI1.cathodeDP, DI2.cathodeDP
  N21: DI1.commAnode#2, R1.Pin_0
  N22: DI1.cathodeF, DI2.cathodeF
  N23: DI2.commAnode#2, R2.Pin_0

notes:
  Arduino Python TkInter Schematic
